// Logisim project rid1_Full (1).circ as structural Verilog: 7 circuits, main circuit main
module main (
  input  [3:0] in_1,
  input  [3:0] in_2,
  input  [3:0] in_3,
  input  [15:0] in_4,
  input  in_5,
  input  in_6,
  output [15:0] out_7,
  output [15:0] out_8
);

  reg_file reg_file_1 (
    .Write_Register(in_3), .read_register_1(in_1), .read_register_2(in_2), .Write_Control(in_5),
    .Write_Data(in_4), .out_7(out_7), .out_8(out_8), .CLK(in_6));
endmodule

module reg_file (
  input  [3:0] Write_Register,
  input  [3:0] read_register_1,
  input  [3:0] read_register_2,
  input  Write_Control,
  input  CLK,
  input  [15:0] Write_Data,
  output [15:0] out_7,
  output [15:0] out_8
);

  wire and_1_out, and_2_out, and_3_out, and_4_out, and_5_out, and_6_out, and_7_out, and_8_out, and_9_out,
       and_10_out, and_11_out, and_12_out, and_13_out, and_14_out, and_15_out, and_16_out, decoder_1_out0,
       decoder_1_out1, decoder_1_out2, decoder_1_out3, decoder_1_out4, decoder_1_out5, decoder_1_out6,
       decoder_1_out7, decoder_1_out8, decoder_1_out9, decoder_1_out10, decoder_1_out11, decoder_1_out12,
       decoder_1_out13, decoder_1_out14, decoder_1_out15;
  wire [15:0] r0_q, r1_q, r2_q, r3_q, r4_q, r5_q, r6_q, r7_q, r8_q, r9_q, r10_q, r11_q, r12_q, r13_q, r14_q,
       r15_q;

  Decoder #(.select(4)) decoder_1 (
    .out0(decoder_1_out0), .out1(decoder_1_out1), .out2(decoder_1_out2), .out3(decoder_1_out3),
    .out4(decoder_1_out4), .out5(decoder_1_out5), .out6(decoder_1_out6), .out7(decoder_1_out7),
    .out8(decoder_1_out8), .out9(decoder_1_out9), .out10(decoder_1_out10), .out11(decoder_1_out11),
    .out12(decoder_1_out12), .out13(decoder_1_out13), .out14(decoder_1_out14), .out15(decoder_1_out15),
    .sel(Write_Register));  // open: en
  and and_1 (and_1_out, decoder_1_out3, Write_Control);
  and and_2 (and_2_out, decoder_1_out4, Write_Control);
  and and_3 (and_3_out, decoder_1_out5, Write_Control);
  and and_4 (and_4_out, decoder_1_out6, Write_Control);
  and and_5 (and_5_out, decoder_1_out7, Write_Control);
  and and_6 (and_6_out, decoder_1_out8, Write_Control);
  and and_7 (and_7_out, decoder_1_out9, Write_Control);
  and and_8 (and_8_out, decoder_1_out10, Write_Control);
  and and_9 (and_9_out, decoder_1_out11, Write_Control);
  and and_10 (and_10_out, decoder_1_out12, Write_Control);
  and and_11 (and_11_out, decoder_1_out13, Write_Control);
  and and_12 (and_12_out, decoder_1_out14, Write_Control);
  and and_13 (and_13_out, decoder_1_out15, Write_Control);
  and and_14 (and_14_out, decoder_1_out0, Write_Control);
  and and_15 (and_15_out, decoder_1_out1, Write_Control);
  and and_16 (and_16_out, decoder_1_out2, Write_Control);
  Register #(.width(16)) r0 (.D(Write_Data), .en(and_14_out), .Q(r0_q), .clk(CLK));  // open: clr
  Register #(.width(16)) r1 (.D(Write_Data), .en(and_15_out), .Q(r1_q), .clk(CLK));  // open: clr
  Register #(.width(16)) r2 (.D(Write_Data), .en(and_16_out), .Q(r2_q), .clk(CLK));  // open: clr
  Register #(.width(16)) r3 (.D(Write_Data), .en(and_1_out), .Q(r3_q), .clk(CLK));  // open: clr
  Register #(.width(16)) r4 (.D(Write_Data), .en(and_2_out), .Q(r4_q), .clk(CLK));  // open: clr
  Register #(.width(16)) r5 (.D(Write_Data), .en(and_3_out), .Q(r5_q), .clk(CLK));  // open: clr
  Register #(.width(16)) r6 (.D(Write_Data), .en(and_4_out), .Q(r6_q), .clk(CLK));  // open: clr
  Register #(.width(16)) r7 (.D(Write_Data), .en(and_5_out), .Q(r7_q), .clk(CLK));  // open: clr
  Register #(.width(16)) r8 (.D(Write_Data), .en(and_6_out), .Q(r8_q), .clk(CLK));  // open: clr
  Register #(.width(16)) r9 (.D(Write_Data), .en(and_7_out), .Q(r9_q), .clk(CLK));  // open: clr
  Register #(.width(16)) r10 (.D(Write_Data), .en(and_8_out), .Q(r10_q), .clk(CLK));  // open: clr
  Register #(.width(16)) r11 (.D(Write_Data), .en(and_9_out), .Q(r11_q), .clk(CLK));  // open: clr
  Register #(.width(16)) r12 (.D(Write_Data), .en(and_10_out), .Q(r12_q), .clk(CLK));  // open: clr
  Register #(.width(16)) r13 (.D(Write_Data), .en(and_11_out), .Q(r13_q), .clk(CLK));  // open: clr
  Register #(.width(16)) r14 (.D(Write_Data), .en(and_12_out), .Q(r14_q), .clk(CLK));  // open: clr
  Register #(.width(16)) r15 (.D(Write_Data), .en(and_13_out), .Q(r15_q), .clk(CLK));  // open: clr
  Multiplexer #(.select(4), .width(16)) multiplexer_1 (
    .in0(r0_q), .in1(r1_q), .in2(r2_q), .in3(r3_q), .in4(r4_q), .in5(r5_q), .in6(r6_q), .in7(r7_q),
    .in8(r8_q), .in9(r9_q), .in10(r10_q), .in11(r11_q), .in12(r12_q), .in13(r13_q), .in14(r14_q),
    .in15(r15_q), .out(out_7), .sel(read_register_1));  // open: en
  Multiplexer #(.select(4), .width(16)) multiplexer_2 (
    .in0(r0_q), .in1(r1_q), .in2(r2_q), .in3(r3_q), .in4(r4_q), .in5(r5_q), .in6(r6_q), .in7(r7_q),
    .in8(r8_q), .in9(r9_q), .in10(r10_q), .in11(r11_q), .in12(r12_q), .in13(r13_q), .in14(r14_q),
    .in15(r15_q), .out(out_8), .sel(read_register_2));  // open: en
endmodule

module _1_bit_alu (
  input  A,
  input  B,
  input  in_3,
  input  [1:0] Select_bit,
  output sum,
  output cout
);

  wire adder_1_out, and_1_out, and_2_out, multiplexer_1_out, not_1_out, or_1_out;

  not not_1 (not_1_out, B);
  Multiplexer multiplexer_1 (.in0(B), .in1(not_1_out), .out(multiplexer_1_out), .sel(and_1_out));  // open: en
  and and_1 (and_1_out, Select_bit[0], Select_bit[1]);
  and and_2 (and_2_out, A, B);
  or or_1 (or_1_out, A, B);
  Adder #(.width(1)) adder_1 (.a(A), .b(multiplexer_1_out), .out(adder_1_out), .cin(in_3), .cout(cout));
  Multiplexer #(.select(2)) multiplexer_2 (
    .in0(and_2_out), .in1(or_1_out), .in2(adder_1_out), .in3(adder_1_out), .out(sum), .sel(Select_bit));  // open: en
endmodule

module _16_bit_alu (
  input  in_1,
  input  [15:0] B,
  input  [15:0] A,
  input  [1:0] in_4,
  output [15:0] out_5,
  output Flag,
  output Overflow,
  output out_8
);

  wire n1_bit_alu_1_cout, n1_bit_alu_2_cout, n1_bit_alu_3_cout, n1_bit_alu_4_cout, n1_bit_alu_5_cout,
       n1_bit_alu_6_cout, n1_bit_alu_7_cout, n1_bit_alu_8_cout, n1_bit_alu_9_cout, n1_bit_alu_10_cout,
       n1_bit_alu_11_cout, n1_bit_alu_12_cout, n1_bit_alu_13_cout, n1_bit_alu_14_cout, n1_bit_alu_15_cout;

  _1_bit_alu u_1_bit_alu_1 (
    .sum(out_5[0]), .in_3(in_1), .Select_bit(in_4), .cout(n1_bit_alu_1_cout), .A(A[0]), .B(B[0]));
  _1_bit_alu u_1_bit_alu_2 (
    .sum(out_5[1]), .in_3(n1_bit_alu_1_cout), .Select_bit(in_4), .cout(n1_bit_alu_2_cout), .A(A[1]), .B(B[1]));
  _1_bit_alu u_1_bit_alu_3 (
    .sum(out_5[2]), .in_3(n1_bit_alu_2_cout), .Select_bit(in_4), .cout(n1_bit_alu_3_cout), .A(A[2]), .B(B[2]));
  _1_bit_alu u_1_bit_alu_4 (
    .sum(out_5[3]), .in_3(n1_bit_alu_3_cout), .Select_bit(in_4), .cout(n1_bit_alu_4_cout), .A(A[3]), .B(B[3]));
  _1_bit_alu u_1_bit_alu_5 (
    .sum(out_5[4]), .in_3(n1_bit_alu_4_cout), .Select_bit(in_4), .cout(n1_bit_alu_5_cout), .A(A[4]), .B(B[4]));
  _1_bit_alu u_1_bit_alu_6 (
    .sum(out_5[5]), .in_3(n1_bit_alu_5_cout), .Select_bit(in_4), .cout(n1_bit_alu_6_cout), .A(A[5]), .B(B[5]));
  _1_bit_alu u_1_bit_alu_7 (
    .sum(out_5[6]), .in_3(n1_bit_alu_6_cout), .Select_bit(in_4), .cout(n1_bit_alu_7_cout), .A(A[6]), .B(B[6]));
  _1_bit_alu u_1_bit_alu_8 (
    .sum(out_5[7]), .in_3(n1_bit_alu_7_cout), .Select_bit(in_4), .cout(n1_bit_alu_8_cout), .A(A[7]), .B(B[7]));
  _1_bit_alu u_1_bit_alu_9 (
    .sum(out_5[8]), .in_3(n1_bit_alu_8_cout), .Select_bit(in_4), .cout(n1_bit_alu_9_cout), .A(A[8]), .B(B[8]));
  _1_bit_alu u_1_bit_alu_10 (
    .sum(out_5[9]), .in_3(n1_bit_alu_9_cout), .Select_bit(in_4), .cout(n1_bit_alu_10_cout), .A(A[9]), .B(B[9]));
  _1_bit_alu u_1_bit_alu_11 (
    .sum(out_5[10]), .in_3(n1_bit_alu_10_cout), .Select_bit(in_4), .cout(n1_bit_alu_11_cout), .A(A[10]),
    .B(B[10]));
  _1_bit_alu u_1_bit_alu_12 (
    .sum(out_5[11]), .in_3(n1_bit_alu_11_cout), .Select_bit(in_4), .cout(n1_bit_alu_12_cout), .A(A[11]),
    .B(B[11]));
  _1_bit_alu u_1_bit_alu_13 (
    .sum(out_5[12]), .in_3(n1_bit_alu_12_cout), .Select_bit(in_4), .cout(n1_bit_alu_13_cout), .A(A[12]),
    .B(B[12]));
  _1_bit_alu u_1_bit_alu_14 (
    .sum(out_5[13]), .Select_bit(in_4), .cout(n1_bit_alu_14_cout), .A(A[13]), .B(B[13]));  // open: in_3
  _1_bit_alu u_1_bit_alu_15 (
    .sum(out_5[14]), .in_3(n1_bit_alu_14_cout), .Select_bit(in_4), .cout(n1_bit_alu_15_cout), .A(A[14]),
    .B(B[14]));
  _1_bit_alu u_1_bit_alu_16 (
    .sum(out_5[15]), .in_3(n1_bit_alu_15_cout), .Select_bit(in_4), .cout(out_8), .A(A[15]), .B(B[15]));
  xor xor_1 (Overflow, n1_bit_alu_15_cout, out_8);
  nor nor_1 (Flag, out_5[0], out_5[1], out_5[2], out_5[3], out_5[4], out_5[5], out_5[6], out_5[7], out_5[8], out_5[9], out_5[10], out_5[11], out_5[12], out_5[13], out_5[14], out_5[15]);

  // Notes on the sheet:
  //   result
  //   Ridwain islam
endmodule

module R_type_Datapath (
  input  in_1,
  input  wc,
  output out_3
);

  wire clock_1_out;
  wire [1:0] bit_extender_1_out;
  wire [15:0] adder_1_out, n16_bit_alu_1_out_5, r0_q, reg_file_1_out_7, reg_file_1_out_8, rom_1_data;

  Clock clock_1 (.out(clock_1_out));
  Register #(.width(16)) r0 (.D(adder_1_out), .Q(r0_q), .clk(clock_1_out));  // open: en, clr
  Adder #(.width(16)) adder_1 (.a(r0_q), .b(16'h1), .out(adder_1_out));  // open: cin, cout
  ROM #(.addrWidth(16), .dataWidth(16)) rom_1 (.addr(r0_q), .data(rom_1_data));  // open: sel
  reg_file reg_file_1 (
    .Write_Register(rom_1_data[3:0]), .read_register_1(rom_1_data[11:8]), .read_register_2(rom_1_data[7:4]),
    .Write_Control(wc), .Write_Data(n16_bit_alu_1_out_5), .out_7(reg_file_1_out_7), .out_8(reg_file_1_out_8),
    .CLK(clock_1_out));
  Bit_Extender #(.in_width(4), .out_width(2)) bit_extender_1 (.in(rom_1_data[15:12]), .out(bit_extender_1_out));
  _16_bit_alu u_16_bit_alu_1 (
    .in_1(in_1), .out_5(n16_bit_alu_1_out_5), .out_8(out_3), .A(reg_file_1_out_7), .B(reg_file_1_out_8),
    .in_4(bit_extender_1_out));  // open: Overflow, Flag

  // Notes on the sheet:
  //   Ridwain Islam
endmodule

module I_type_Datapath (
  input  in_1,
  input  wc,
  input  Sc,
  input  Lc,
  output out_5
);

  wire clk_out;
  wire [1:0] bit_extender_1_out;
  wire [15:0] adder_1_out, bit_extender_2_out, n16_bit_alu_1_out_5, r0_q, ram_1_data, reg_file_1_out_7,
       reg_file_1_out_8, rom_1_data;

  Clock clk (.out(clk_out));
  Register #(.width(16)) r0 (.D(adder_1_out), .Q(r0_q), .clk(clk_out));  // open: en, clr
  Adder #(.width(16)) adder_1 (.a(r0_q), .b(16'h1), .out(adder_1_out));  // open: cin, cout
  ROM #(.addrWidth(16), .dataWidth(16)) rom_1 (.addr(r0_q), .data(rom_1_data));  // open: sel
  reg_file reg_file_1 (
    .Write_Register(rom_1_data[7:4]), .read_register_1(rom_1_data[11:8]), .read_register_2(rom_1_data[7:4]),
    .Write_Control(wc), .Write_Data(ram_1_data), .out_7(reg_file_1_out_7), .out_8(reg_file_1_out_8),
    .CLK(clk_out));
  Bit_Extender #(.in_width(4), .out_width(2)) bit_extender_1 (.in(rom_1_data[15:12]), .out(bit_extender_1_out));
  assign bit_extender_2_out = {{12{1'b0}}, rom_1_data[3:0]};  // Bit_Extender bit_extender_2
  _16_bit_alu u_16_bit_alu_1 (
    .in_1(in_1), .out_5(n16_bit_alu_1_out_5), .out_8(out_5), .A(reg_file_1_out_7), .B(bit_extender_2_out),
    .in_4(bit_extender_1_out));  // open: Overflow, Flag
  RAM #(.addrWidth(16), .dataWidth(16), .bus("separate")) ram_1 (
    .addr(n16_bit_alu_1_out_5), .din(reg_file_1_out_8), .data(ram_1_data), .str(Sc), .clk(clk_out), .ld(Lc));  // open: sel, clr

  // Notes on the sheet:
  //   Ridwain Islam
endmodule

module Datapath (
  input  in_1,
  input  wc,
  input  Sc,
  input  Lc,
  input  Lc_2,
  output Cout
);

  wire clk_out;
  wire [1:0] bit_extender_1_out;
  wire [3:0] multiplexer_1_out;
  wire [15:0] adder_1_out, bit_extender_2_out, multiplexer_2_out, multiplexer_3_out, n16_bit_alu_1_out_5,
       r0_q, ram_1_data, reg_file_1_out_7, reg_file_1_out_8, rom_1_data;

  Clock clk (.out(clk_out));
  Register #(.width(16)) r0 (.D(adder_1_out), .Q(r0_q), .clk(clk_out));  // open: en, clr
  Adder #(.width(16)) adder_1 (.a(r0_q), .b(16'h1), .out(adder_1_out));  // open: cin, cout
  ROM #(.addrWidth(16), .dataWidth(16)) rom_1 (.addr(r0_q), .data(rom_1_data));  // open: sel
  Multiplexer #(.width(4)) multiplexer_1 (
    .in0(rom_1_data[3:0]), .in1(rom_1_data[7:4]), .out(multiplexer_1_out), .sel(Lc_2));  // open: en
  reg_file reg_file_1 (
    .Write_Register(multiplexer_1_out), .read_register_1(rom_1_data[11:8]),
    .read_register_2(rom_1_data[7:4]), .Write_Control(wc), .Write_Data(multiplexer_3_out),
    .out_7(reg_file_1_out_7), .out_8(reg_file_1_out_8), .CLK(clk_out));
  Bit_Extender #(.in_width(4), .out_width(2)) bit_extender_1 (.in(rom_1_data[15:12]), .out(bit_extender_1_out));
  assign bit_extender_2_out = {{12{1'b0}}, rom_1_data[3:0]};  // Bit_Extender bit_extender_2
  Multiplexer #(.width(16)) multiplexer_2 (
    .in0(reg_file_1_out_8), .in1(bit_extender_2_out), .out(multiplexer_2_out), .sel(Lc_2));  // open: en
  _16_bit_alu u_16_bit_alu_1 (
    .in_1(in_1), .out_5(n16_bit_alu_1_out_5), .out_8(Cout), .A(reg_file_1_out_7), .B(multiplexer_2_out),
    .in_4(bit_extender_1_out));  // open: Overflow, Flag
  RAM #(.addrWidth(16), .dataWidth(16), .bus("separate")) ram_1 (
    .addr(n16_bit_alu_1_out_5), .din(reg_file_1_out_8), .data(ram_1_data), .str(Sc), .clk(clk_out), .ld(Lc));  // open: sel, clr
  Multiplexer #(.width(16)) multiplexer_3 (
    .in0(n16_bit_alu_1_out_5), .in1(ram_1_data), .out(multiplexer_3_out), .sel(Lc_2));  // open: en

  // Notes on the sheet:
  //   Ridwain Islam
endmodule
